# Fritzing sketch pyWheater (saved by Fritzing 0.9.3b)
circuit board: 8.46667cm x 5.64444cm
breadboards: 1

parts:
  RHT2 = Humidity and Temperature Sensor RHT03
  Bauteil1 = Adafruit CCS811
  Bauteil4 = Adafruit T-Cobbler Plus [part_number="Adafruit #1989 and #2028"]
  R1 = Resistor [tolerance=±5% resistance=10k package=THT]
  Waveshare_LCD_display = Adafruit Pi Cobbler Plus [part_number="Adafruit #2029"]
  MCU1 = Raspberry Pi Zero

nets:
  +3.3V: RHT2.Vcc, Bauteil1.VIN, Bauteil4.+3.3V, R1.Pin_1, Waveshare_LCD_display.+3.3V, MCU1.pin_1, MCU1.pin_17
  N1: RHT2.Data-signal, Bauteil4.GPIO22, R1.Pin_0, MCU1.pin_15
  GND: RHT2.GND_2, Bauteil1.GND, Bauteil1.!WAKE, Bauteil4.GND, Waveshare_LCD_display.GND, MCU1.pin_6, MCU1.pin_9, MCU1.pin_39
  N2: Bauteil1.SDA, Bauteil4.SDA, MCU1.pin_3
  N3: Bauteil1.SCL, Bauteil4.SCL, MCU1.pin_5
  +5V: Bauteil4.+5V, Waveshare_LCD_display.+5V, MCU1.pin_2, MCU1.pin_4
  N4: Waveshare_LCD_display.MOSI, MCU1.pin_19
  N5: Waveshare_LCD_display.MISO, MCU1.pin_21
  N6: Waveshare_LCD_display.SCLK, MCU1.pin_23
  N7: Waveshare_LCD_display.GPIO18, MCU1.pin_12
  N8: Waveshare_LCD_display.GPIO25, MCU1.pin_22
  N9: Waveshare_LCD_display.CE1, MCU1.pin_26

custom parts:
  Adafruit T-Cobbler Plus: The Raspberry Pi has landed on the Maker World like a 40-GPIO pinned, quad-USB ported, credit card sized bomb of DIY joy. And while you can use most of our great Model B accessories by hooking up our downgrade cable, its probably a good time to upgrade your set up and accessorize using all of the 40 pins. That's why we now carry the Assembled Adafruit Pi T-Cobbler Plus - Breakout + Cable for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
  Adafruit Pi Cobbler Plus: The Raspberry Pi B+/Pi 2/ Pi 3 has landed on the Maker World like a 40-GPIO pinned, quad-USB ported, credit card sized bomb of DIY joy. And while you can use most of our great Model B accessories by hooking up our downgrade cable, its probably a good time to upgrade your set up and accessorize using all of the Model B+'s / Pi 2's / Pi 3's 40 pins. That's why we now carry the Adafruit Assembled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
